# Fritzing sketch TheLivingPlant_Connectivity (saved by Fritzing 0.9.3b)

parts:
  M2 = Spresense ext board
  RHT1 = Humidity and Temperature Sensor RHT03
  Part1 = Soil Moisture Sensor
  R1 = Photocell (LDR) [package=THT]
  SP1 = SPEAKER [package=pcb_mount_speaker]  # not connected
  J1 = Camdenboss CTB0158-8 [part_number=CTB0158-8 package=THT]
  J2 = Camdenboss CTB0158-8 [part_number=CTB0158-8 package=THT]
  LED2 = RGB LED (com. anode, rbg) [package="5 mm [THT]"]
  U1 = RELAY [package=relay-jzc]
  Power_plug1 = Power plug
  J3 = JST-VHR-3N [part_number=JST-VHR-3N package=THT]
  J4 = JST-B3P-VH [part_number=JST-B3P-VH package=THT]
  U2 = ESP8266 WiFi Module [part_number=ESP8266]

nets:
  N1: M2.RST, M2.3.3V, J1.pin6
  N2: M2.GND, J2.pin5
  N3: M2.A52, Part1.SIG
  N4: M2.A1, J4.pin3
  N5: M2.A2, R1.pin_1, J3.pin3, J3.pin_6
  N6: M2.RX_0, U2.RX
  N7: M2.TX_1, U2.TX
  N8: M2.PWM_6, M2.7, RHT1.Data-signal
  N9: M2.8, LED2.blue_cathode
  N10: M2.9, LED2.green_cathode
  N11: M2.10, LED2.red_cathode
  N12: RHT1.Vcc, J1.pin3
  N13: RHT1.GND_1, RHT1.GND_2, J2.pin2
  N14: Part1.GND, J2.pin1
  N15: Part1.VCC, J1.pin2
  N16: J1.pin1, U1.NC, U1.NO
  N17: J1.pin4, J4.pin1
  N18: J1.pin5, J3.pin1, J3.pin_4
  N19: J1.pin8, U2.3.3V
  N20: J2.pin3, J4.pin2
  N21: J2.pin4, J3.pin2
  N22: J2.pin6, U1.COIL2
  N23: J2.pin8, U2.GND
  N24: U1.MAIN, Power_plug1.VCC
  N25: U1.COIL1, Power_plug1.GND

notes:
  Water pump
  Air Sensor
  Light
  Temperature
  Relay
  Speaker
  RGB Led
  Wifi ESP8266
  Soil
  GND
  VCC
